# Fritzing sketch esp32-led (saved by Fritzing 0.9.4)
breadboards: 2

parts:
  R1 = Resistor [tolerance=±5% resistance=100 package="0805 [SMD]"]
  U1 = LuaNode32 / ESP32
  LED1 = LED - 3mm [color="Red (633nm)" package="3 mm [THT]"]

nets:
  N1: R1.Pin_0, LED1.cathode
  N2: R1.Pin_1, U1.D5
  N3: U1.GND, LED1.anode

custom parts:
  LuaNode32 / ESP32: ESP32 based LuaNode32
